# Fritzing sketch LCD VU Meter (saved by Fritzing 0.9.4)
breadboards: 1

parts:
  Part1 = Arduino Uno (Rev3)
  Part2 = LCD1602-I2C
  R1 = Resistor [tolerance=±1% resistance=22k package=THT]
  R2 = Resistor [tolerance=±1% resistance=100k package=THT]
  R3 = Resistor [tolerance=±1% resistance=100k package=THT]
  R4 = Resistor [tolerance=±1% resistance=100k package=THT]
  R5 = Resistor [tolerance=±1% resistance=100k package=THT]
  C1 = Ceramic Capacitor [capacitance=100nF package="100 mil [THT, multilayer]"]
  C2 = Ceramic Capacitor [capacitance=100nF package="100 mil [THT, multilayer]"]
  TRS1 = Audio Jack (TRS) 3.5mm [package="4Ucon 08780 [THT]"]

nets:
  N1: Part1.A2, R3.Pin_1, R4.Pin_0, C2.1
  N2: Part1.A3, R2.Pin_1, R5.Pin_0, C1.0
  GND: Part1.GND, Part2.GND, R4.Pin_1, R5.Pin_1, TRS1.Sleeve
  N3: Part1.AREF, R1.Pin_1, R2.Pin_0, R3.Pin_0
  N4: Part1.A4/SDA, Part2.SDA
  N5: Part1.A5/SCL, Part2.SCL
  N6: Part1.3V3, R1.Pin_0
  5V: Part1.5V, Part2.VCC
  N7: C1.1, TRS1.Tip
  N8: C2.0, TRS1.Ring

custom parts:
  LCD1602-I2C: A standard character display, usually with 2x16 characters. Comes in many colors with LCM1602 IIC attached.
